# Fritzing sketch Basketball (saved by Fritzing 0.9.3b)
breadboards: 1

parts:
  Part1 = Arduino Uno (Rev3) - ICSP
  J1 = Piezo Speaker
  R1 = Basic Flex Resistor
  R2 = Resistor [tolerance=±5% resistance=10k package="0805 [SMD]"]
  S1 = Round Pushbutton
  LCD1 = Serial Enabled 16x2 LCD - Black on Green 5V [part_number=LCD-09393]
  S2 = Toggle Switch [package=THT]
  VCC1 = Battery block 9V

nets:
  N1: Part1.A0, R1.Pin_2, R2.Pin_0
  N2: Part1.D9_PWM, J1.pin2
  N3: Part1.D2, LCD1.RX
  N4: Part1.D7, S1.leg1
  5V: Part1.5V, R2.Pin_1, LCD1.VDD
  GND: Part1.GND, J1.pin1, R1.pin_1, S1.leg0, LCD1.GND, VCC1.-
  N5: Part1.VIN, S2.COM
  N6: S2.L1, VCC1.+

notes:
  VDD
  GND
  RX

custom parts:
  Serial Enabled 16x2 LCD - Black on Green 5V: This is the latest evolution of our serial LCD. Included on a single board is a 16x2 LCD and an embedded circuit based around a PIC 16F88. The on-board PIC takes a TTL serial input and prints the characters it receives onto the LCD. The installed firmware also allows for a number of special commands so you can clear the screen, adjust the backlight brightness, turn the display on/off, and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
